# Fritzing sketch 基本電路_1LED_PWM (saved by Fritzing 0.9.2b)
breadboards: 1

parts:
  Ameba1 = Ameba
  R1 = Resistor [tolerance=±5% resistance=220 package=THT]
  LED1 = LED - 5mm [color="Red (633nm)" package="5 mm [THT]"]

nets:
  N1: Ameba1.D11, LED1.anode
  N2: Ameba1.GND, R1.Pin_0
  N3: R1.Pin_1, LED1.cathode

notes:
  220 ohm
  220 歐姆
  D11
  LED Anode
  陽極

custom parts:
  Ameba: Ameba EVB
