# Fritzing sketch 基本電路_2LED_PWM (saved by Fritzing 0.9.2b)
breadboards: 1

parts:
  Ameba1 = Ameba
  R1 = Resistor [tolerance=±5% resistance=220 package=THT]
  LED1 = LED - 5mm [color="Red (633nm)" package="5 mm [THT]"]
  R2 = Resistor [tolerance=±5% resistance=220 package=THT]
  LED2 = LED - 5mm [color="Red (633nm)" package="5 mm [THT]"]

nets:
  N1: Ameba1.D11, LED1.anode
  N2: Ameba1.D12, LED2.anode
  N3: Ameba1.GND, R1.Pin_0, R2.Pin_0
  N4: R1.Pin_1, LED2.cathode
  N5: LED1.cathode, R2.Pin_1

notes:
  LED2
  D12
  LED1
  D11
  220 ohm
  220 歐姆
  LED Anode
  陽極

custom parts:
  Ameba: Ameba EVB
