# Fritzing sketch 基本電路_4Led (saved by Fritzing 0.9.2b)
breadboards: 1

parts:
  元件1 = Arduino Mega 2560 (Rev3)
  R3 = Resistor [tolerance=±5% resistance=220 package=THT]
  R4 = Resistor [tolerance=±5% resistance=220 package=THT]
  R5 = Resistor [tolerance=±5% resistance=220 package=THT]
  R6 = Resistor [tolerance=±5% resistance=220 package=THT]
  LED5 = LED - 5mm [color="Red (633nm)" package="5 mm [THT]"]
  LED6 = LED - 5mm [color="Red (633nm)" package="5 mm [THT]"]
  LED7 = LED - 5mm [color="Red (633nm)" package="5 mm [THT]"]
  LED8 = LED - 5mm [color="Red (633nm)" package="5 mm [THT]"]

nets:
  N1: 元件1.GND, LED5.anode, LED6.anode, LED7.anode, LED8.anode
  N2: 元件1.D4_PWM, R5.Pin_1
  N3: 元件1.D5_PWM, R6.Pin_1
  N4: 元件1.D6_PWM, R3.Pin_1
  N5: 元件1.D7_PWM, R4.Pin_1
  N6: R3.Pin_0, LED6.cathode
  N7: R4.Pin_0, LED5.cathode
  N8: R5.Pin_0, LED8.cathode
  N9: R6.Pin_0, LED7.cathode
