# Fritzing sketch 基本電路_6Led (saved by Fritzing 0.9.2b)
breadboards: 1

parts:
  元件1 = Arduino Mega 2560 (Rev3)
  R1 = Resistor [tolerance=±5% resistance=220 package=THT]
  R2 = Resistor [tolerance=±5% resistance=220 package=THT]
  R3 = Resistor [tolerance=±5% resistance=220 package=THT]
  R4 = Resistor [tolerance=±5% resistance=220 package=THT]
  R6 = Resistor [tolerance=±5% resistance=220 package=THT]
  R7 = Resistor [tolerance=±5% resistance=220 package=THT]
  LED2 = LED - 5mm [color="Red (633nm)" package="5 mm [THT]"]
  LED3 = LED - 5mm [color="Red (633nm)" package="5 mm [THT]"]
  LED4 = LED - 5mm [color="Red (633nm)" package="5 mm [THT]"]
  LED5 = LED - 5mm [color="Red (633nm)" package="5 mm [THT]"]
  LED6 = LED - 5mm [color="Red (633nm)" package="5 mm [THT]"]
  LED7 = LED - 5mm [color="Red (633nm)" package="5 mm [THT]"]

nets:
  N1: 元件1.D10_PWM, R7.Pin_1
  N2: 元件1.D9_PWM, R1.Pin_1
  N3: 元件1.D8_PWM, R2.Pin_1
  N4: 元件1.GND, LED2.anode, LED3.anode, LED4.anode, LED5.anode, LED6.anode, LED7.anode
  N5: 元件1.D5_PWM, R6.Pin_1
  N6: 元件1.D6_PWM, R3.Pin_1
  N7: 元件1.D7_PWM, R4.Pin_1
  N8: R1.Pin_0, LED3.cathode
  N9: R2.Pin_0, LED4.cathode
  N10: R3.Pin_0, LED6.cathode
  N11: R4.Pin_0, LED5.cathode
  N12: R6.Pin_0, LED7.cathode
  N13: R7.Pin_0, LED2.cathode
