# Fritzing sketch 基本電路_8Led_Button (saved by Fritzing 0.9.2b)
breadboards: 1

parts:
  元件1 = Arduino Mega 2560 (Rev3)
  R1 = Resistor [tolerance=±5% resistance=220 package=THT]
  R2 = Resistor [tolerance=±5% resistance=220 package=THT]
  R3 = Resistor [tolerance=±5% resistance=220 package=THT]
  R4 = Resistor [tolerance=±5% resistance=220 package=THT]
  R5 = Resistor [tolerance=±5% resistance=220 package=THT]
  R6 = Resistor [tolerance=±5% resistance=220 package=THT]
  R7 = Resistor [tolerance=±5% resistance=220 package=THT]
  R8 = Resistor [tolerance=±5% resistance=220 package=THT]
  LED1 = LED - 5mm [color="Red (633nm)" package="5 mm [THT]"]
  LED2 = LED - 5mm [color="Red (633nm)" package="5 mm [THT]"]
  LED3 = LED - 5mm [color="Red (633nm)" package="5 mm [THT]"]
  LED4 = LED - 5mm [color="Red (633nm)" package="5 mm [THT]"]
  LED5 = LED - 5mm [color="Red (633nm)" package="5 mm [THT]"]
  LED6 = LED - 5mm [color="Red (633nm)" package="5 mm [THT]"]
  LED7 = LED - 5mm [color="Red (633nm)" package="5 mm [THT]"]
  LED8 = LED - 5mm [color="Red (633nm)" package="5 mm [THT]"]
  S1 = Pushbutton [package="[SMD]"]
  R9 = Resistor [tolerance=±5% resistance=220 package=THT]

nets:
  N1: 元件1.D11_PWM, R8.Pin_1
  N2: 元件1.D10_PWM, R7.Pin_1
  N3: 元件1.D9_PWM, R1.Pin_1
  N4: 元件1.D8_PWM, R2.Pin_1
  N5: 元件1.GND, LED1.anode, LED2.anode, LED3.anode, LED4.anode, LED5.anode, LED6.anode, LED7.anode, LED8.anode, S1.Pin_1, S1.Pin_2
  N6: 元件1.D2_PWM, S1.Pin_3, S1.Pin_4, R9.Pin_1
  N7: 元件1.D4_PWM, R5.Pin_1
  N8: 元件1.D5_PWM, R6.Pin_1
  N9: 元件1.D6_PWM, R3.Pin_1
  N10: 元件1.D7_PWM, R4.Pin_1
  N11: R1.Pin_0, LED3.cathode
  N12: R2.Pin_0, LED4.cathode
  N13: R3.Pin_0, LED6.cathode
  N14: R4.Pin_0, LED5.cathode
  N15: R5.Pin_0, LED8.cathode
  N16: R6.Pin_0, LED7.cathode
  N17: R7.Pin_0, LED2.cathode
  N18: R8.Pin_0, LED1.cathode
