# Fritzing sketch 基本電路_BLE4 (saved by Fritzing 0.9.2b)
breadboards: 1

parts:
  Ameba1 = Ameba
  Part2 = Adafruit Bluefruit LE UART Friend [part_number="Adafruit #2479"]

nets:
  N1: Ameba1.D0, Part2.TXO
  N2: Ameba1.D1, Part2.RXI
  GND: Ameba1.GND, Part2.GND
  5V: Ameba1.5V, Part2.VIN

custom parts:
  Ameba: Ameba EVB
  Adafruit Bluefruit LE UART Friend: The Bluefruit LE UART Friend makes it easy to add Bluetooth Low Energy connectivity to anything with a hardware or software serial port. We even have nice hardware flow control so you won't have to think about losing data. Connect to your Arduino or other microcontroller or even just a standard FTDI cable for debugging and testing.
