# Fritzing sketch 基本電路_BT_LCD1602_RGBLed (saved by Fritzing 0.9.2b)
breadboards: 1

parts:
  Ameba1 = Ameba
  LCM1602_IIC3 = LCM1602 IIC [part_number="LCM1602 IIC" chip_label="LCM1602 IIC" package="DIP (Dual Inline) [THT]"]
  LCD1 = LCD screen
  LED9 = RGB LED (com. cathode, rbg) [package="5 mm [THT]"]
  R2 = Resistor [tolerance=±5% resistance=220 package=THT]
  R3 = Resistor [tolerance=±5% resistance=220 package=THT]
  R4 = Resistor [tolerance=±5% resistance=220 package=THT]
  Part3 = Bluetooth HC-05 Macho

nets:
  N1: Ameba1.D0, Part3.TXD
  N2: Ameba1.D1, Part3.RXD
  N3: Ameba1.D10, R2.Pin_1
  N4: Ameba1.D11, R3.Pin_1
  N5: Ameba1.D12, R4.Pin_1
  N6: Ameba1.SCL, LCM1602_IIC3.SCL
  N7: Ameba1.SDA, LCM1602_IIC3.SDA
  GND: Ameba1.GND, LCM1602_IIC3.GND, LED9.common_cathode, Part3.GND
  VCC: Ameba1.5V, LCM1602_IIC3.VCC, Part3.VCC
  VSS: LCM1602_IIC3.VSS, LCD1.VSS
  VDD: LCM1602_IIC3.VDD, LCD1.VDD
  N8: LCM1602_IIC3.V0, LCD1.V0
  N9: LCM1602_IIC3.RS, LCD1.RS
  N10: LCM1602_IIC3.RW, LCD1.R/W
  N11: LCM1602_IIC3.E, LCD1.E
  N12: LCM1602_IIC3.D0, LCD1.DB0
  N13: LCM1602_IIC3.D1, LCD1.DB1
  N14: LCM1602_IIC3.D2, LCD1.DB2
  N15: LCM1602_IIC3.D3, LCD1.DB3
  N16: LCM1602_IIC3.D4, LCD1.DB4
  N17: LCM1602_IIC3.D5, LCD1.DB5
  N18: LCM1602_IIC3.D6, LCD1.DB6
  N19: LCM1602_IIC3.D7, LCD1.DB7
  N20: LCM1602_IIC3.A, LCD1.LED+
  N21: LCM1602_IIC3.K, LCD1.LED-
  N22: LCM1602_IIC3.LED_A, LCM1602_IIC3.LED_B

notes:
  全彩LED
  紅綠藍三色
  共陰極
  220歐姆電阻
  HC-05藍芽裝置

custom parts:
  Ameba: Ameba EVB
  LCM1602 IIC: I2C-Module to use a 1602 or 2004 LCD on with the wire.h libory Serial LCD Modul
