# Fritzing sketch 基本電路_DHT11 (saved by Fritzing 0.9.2b)
breadboards: 1

parts:
  Ameba1 = Ameba
  DHT2 = DHT11 Humitidy and Temperature Sensor

nets:
  N1: Ameba1.D7, DHT2.DATA
  GND: Ameba1.GND, DHT2.GND
  N2: Ameba1.5V, DHT2.NULL

custom parts:
  Ameba: Ameba EVB
  DHT11 Humitidy and Temperature Sensor: DHT11 Humidity and Temperature Sensor
