# Fritzing sketch 基本電路_Joystick (saved by Fritzing 0.9.2b)
breadboards: 1

parts:
  Ameba1 = Ameba
  元件1 = Thumb Joystick

nets:
  N1: Ameba1.A2, 元件1.VERT
  N2: Ameba1.A1, 元件1.HORZ
  GND: Ameba1.GND, 元件1.GND
  5V: Ameba1.5V, 元件1.VCC

notes:
  VRy
  Yellow
  A2
  VRx
  Blue
  A1

custom parts:
  Ameba: Ameba EVB
