# Fritzing sketch 基本電路_Joystick_2PWM (saved by Fritzing 0.9.2b)
breadboards: 1

parts:
  Ameba1 = Ameba
  元件1 = Thumb Joystick
  R1 = Resistor [tolerance=±5% resistance=220 package=THT]
  LED1 = LED - 5mm [color="Red (633nm)" package="5 mm [THT]"]
  R2 = Resistor [tolerance=±5% resistance=220 package=THT]
  LED2 = LED - 5mm [color="Red (633nm)" package="5 mm [THT]"]

nets:
  N1: Ameba1.D12, LED1.anode
  N2: Ameba1.D13, LED2.anode
  N3: Ameba1.A2, 元件1.VERT
  N4: Ameba1.A1, 元件1.HORZ
  GND: Ameba1.GND, 元件1.GND
  5V: Ameba1.5V, 元件1.VCC, R1.Pin_0, R2.Pin_0
  N5: R1.Pin_1, LED1.cathode
  N6: R2.Pin_1, LED2.cathode

notes:
  VRx
  Blue
  A1
  Led1
  D11
  Led2
  D12
  220 ohm
  220 歐姆
  LED Anode
  陽極
  VRy
  Yellow
  A2

custom parts:
  Ameba: Ameba EVB
