# Fritzing sketch 基本電路_LCD1602_Duel_Led (saved by Fritzing 0.9.2b)
breadboards: 1

parts:
  Ameba1 = Ameba
  LCM1602_IIC3 = LCM1602 IIC [part_number="LCM1602 IIC" chip_label="LCM1602 IIC" package="DIP (Dual Inline) [THT]"]
  LCD1 = LCD screen
  LED8 = DUO LED RG [package="5 mm [THT]"]

nets:
  N1: Ameba1.D8, LED8.green_anode
  N2: Ameba1.D9, LED8.red_anode
  N3: Ameba1.SCL, LCM1602_IIC3.SCL
  N4: Ameba1.SDA, LCM1602_IIC3.SDA
  GND: Ameba1.GND, LCM1602_IIC3.GND, LED8.common_cathode
  5V: Ameba1.5V, LCM1602_IIC3.VCC
  VSS: LCM1602_IIC3.VSS, LCD1.VSS
  VDD: LCM1602_IIC3.VDD, LCD1.VDD
  N5: LCM1602_IIC3.V0, LCD1.V0
  N6: LCM1602_IIC3.RS, LCD1.RS
  N7: LCM1602_IIC3.RW, LCD1.R/W
  N8: LCM1602_IIC3.E, LCD1.E
  N9: LCM1602_IIC3.D0, LCD1.DB0
  N10: LCM1602_IIC3.D1, LCD1.DB1
  N11: LCM1602_IIC3.D2, LCD1.DB2
  N12: LCM1602_IIC3.D3, LCD1.DB3
  N13: LCM1602_IIC3.D4, LCD1.DB4
  N14: LCM1602_IIC3.D5, LCD1.DB5
  N15: LCM1602_IIC3.D6, LCD1.DB6
  N16: LCM1602_IIC3.D7, LCD1.DB7
  N17: LCM1602_IIC3.A, LCD1.LED+
  N18: LCM1602_IIC3.K, LCD1.LED-
  N19: LCM1602_IIC3.LED_A, LCM1602_IIC3.LED_B

notes:
  雙色LED
  紅綠雙色
  共陰極

custom parts:
  Ameba: Ameba EVB
  LCM1602 IIC: I2C-Module to use a 1602 or 2004 LCD on with the wire.h libory Serial LCD Modul
