# Fritzing sketch 基本電路_Led_Light(D8) (saved by Fritzing 0.9.2b)
breadboards: 1

parts:
  R4 = Resistor [tolerance=±5% resistance=220 package=THT]
  LED5 = LED - 5mm [color="Red (633nm)" package="5 mm [THT]"]
  Ameba2 = Ameba

nets:
  N1: R4.Pin_0, LED5.cathode
  N2: R4.Pin_1, Ameba2.D8
  N3: LED5.anode, Ameba2.GND

custom parts:
  Ameba: Ameba EVB
