# Fritzing sketch 基本電路_MQ2 (saved by Fritzing 0.9.2b)
breadboards: 1

parts:
  Ameba1 = Ameba
  U3 = GAS_SENSOR [package=mq-3]

nets:
  N1: Ameba1.A1, U3.B1
  N2: Ameba1.GND, U3.A1

notes:
  MQ2 Sensor

custom parts:
  Ameba: Ameba EVB
