# Fritzing sketch 基本電路_RGB_Led (saved by Fritzing 0.9.2b)
breadboards: 1

parts:
  Ameba1 = Ameba
  LED1 = RGB LED (com. anode, rbg) [package="5 mm [THT]"]

nets:
  N1: Ameba1.D11, LED1.blue_cathode
  N2: Ameba1.D12, LED1.green_cathode
  N3: Ameba1.GND, LED1.common_anode

notes:
  RGB LED
  共陰
  請使用PWM

custom parts:
  Ameba: Ameba EVB
