# Fritzing sketch 基本電路_RGB_Led_by_Bluetooth (saved by Fritzing 0.9.2b)
breadboards: 1

parts:
  Ameba1 = Ameba
  LED1 = RGB LED (com. anode, rbg) [package="5 mm [THT]"]
  Part3 = Bluetooth HC-05 Macho

nets:
  N1: Ameba1.D0, Part3.TXD
  N2: Ameba1.D1, Part3.RXD
  N3: Ameba1.D11, LED1.blue_cathode
  N4: Ameba1.D12, LED1.green_cathode
  GND: Ameba1.GND, LED1.common_anode, Part3.GND
  5V: Ameba1.5V, Part3.VCC

custom parts:
  Ameba: Ameba EVB
