# Fritzing sketch 基本電路_RTC_DHT (saved by Fritzing 0.9.2b)
breadboards: 1

parts:
  Ameba1 = Ameba
  Tiny_RTC2 = Tiny RTC
  DHT2 = DHT11 Humitidy and Temperature Sensor

nets:
  N1: Ameba1.D3, Tiny_RTC2.SDA
  N2: Ameba1.D4, Tiny_RTC2.SCL
  N3: Ameba1.D7, DHT2.DATA
  GND: Ameba1.GND, Tiny_RTC2.GND, DHT2.GND
  5V: Ameba1.5V, Tiny_RTC2.VCC, DHT2.NULL

custom parts:
  Ameba: Ameba EVB
  Tiny RTC: Tiny RTC I2C module DS1370Z RTC and AT24C32 EEPROM
  DHT11 Humitidy and Temperature Sensor: DHT11 Humidity and Temperature Sensor
