# Fritzing sketch 基本電路_RTC_DHT_LCD (saved by Fritzing 0.9.2b)
breadboards: 1

parts:
  Ameba1 = Ameba
  Tiny_RTC2 = Tiny RTC
  DHT2 = DHT11 Humitidy and Temperature Sensor
  LCM1602_IIC4 = LCM1602 IIC [part_number="LCM1602 IIC" chip_label="LCM1602 IIC" package="DIP (Dual Inline) [THT]"]
  LCD5 = LCD 20x04

nets:
  N1: Ameba1.D3, Tiny_RTC2.SDA
  N2: Ameba1.D4, Tiny_RTC2.SCL
  N3: Ameba1.D7, DHT2.DATA
  N4: Ameba1.SCL, LCM1602_IIC4.SCL
  N5: Ameba1.SDA, LCM1602_IIC4.SDA
  GND: Ameba1.GND, Tiny_RTC2.GND, DHT2.GND, LCM1602_IIC4.GND
  VCC: Ameba1.5V, Tiny_RTC2.VCC, DHT2.NULL, LCM1602_IIC4.VCC
  VSS: LCM1602_IIC4.VSS, LCD5.VSS
  VDD: LCM1602_IIC4.VDD, LCD5.VDD
  N6: LCM1602_IIC4.V0, LCD5.V0
  N7: LCM1602_IIC4.RS, LCD5.RS
  N8: LCM1602_IIC4.RW, LCD5.R/W
  N9: LCM1602_IIC4.E, LCD5.E
  N10: LCM1602_IIC4.D0, LCD5.DB0
  N11: LCM1602_IIC4.D1, LCD5.DB1
  N12: LCM1602_IIC4.D2, LCD5.DB2
  N13: LCM1602_IIC4.D3, LCD5.DB3
  N14: LCM1602_IIC4.D4, LCD5.DB4
  N15: LCM1602_IIC4.D5, LCD5.DB5
  N16: LCM1602_IIC4.D6, LCD5.DB6
  N17: LCM1602_IIC4.D7, LCD5.DB7
  N18: LCM1602_IIC4.A, LCD5.LED+
  N19: LCM1602_IIC4.K, LCD5.LED-
  N20: LCM1602_IIC4.LED_A, LCM1602_IIC4.LED_B

custom parts:
  Ameba: Ameba EVB
  Tiny RTC: Tiny RTC I2C module DS1370Z RTC and AT24C32 EEPROM
  DHT11 Humitidy and Temperature Sensor: DHT11 Humidity and Temperature Sensor
  LCM1602 IIC: I2C-Module to use a 1602 or 2004 LCD on with the wire.h libory Serial LCD Modul
  LCD 20x04: LCD character display, 20 characters by 4 rows. Green.
