# Fritzing sketch 基本電路_RTC_DHT_LCD_LED (saved by Fritzing 0.9.2b)
breadboards: 2

parts:
  Ameba1 = Ameba
  Tiny_RTC2 = Tiny RTC
  DHT2 = DHT11 Humitidy and Temperature Sensor
  LCM1602_IIC4 = LCM1602 IIC [part_number="LCM1602 IIC" chip_label="LCM1602 IIC" package="DIP (Dual Inline) [THT]"]
  LCD5 = LCD 20x04
  LED1 = LED - 5mm [color="Green (570nm)" package="5 mm [THT]"]
  R1 = Resistor [tolerance=±5% resistance=220 package=THT]
  LED2 = LED - 5mm [color="Blue (525nm)" package="5 mm [THT]"]
  LED3 = LED - 5mm [color="Orange (605nm)" package="5 mm [THT]"]
  LED4 = LED - 5mm [color="Red (633nm)" package="5 mm [THT]"]
  LED5 = LED - 5mm [color="Red (633nm)" package="5 mm [THT]"]
  R2 = Resistor [tolerance=±5% resistance=220 package=THT]
  R3 = Resistor [tolerance=±5% resistance=220 package=THT]
  R4 = Resistor [tolerance=±5% resistance=220 package=THT]
  R5 = Resistor [tolerance=±5% resistance=220 package=THT]

nets:
  N1: Ameba1.D3, Tiny_RTC2.SDA
  N2: Ameba1.D4, Tiny_RTC2.SCL
  N3: Ameba1.D7, DHT2.DATA
  N4: Ameba1.D9, R2.Pin_0
  N5: Ameba1.D10, R3.Pin_0
  N6: Ameba1.D11, R4.Pin_0
  N7: Ameba1.SCL, LCM1602_IIC4.SCL
  N8: Ameba1.SDA, LCM1602_IIC4.SDA
  GND: Ameba1.GND, Tiny_RTC2.GND, DHT2.GND, LCM1602_IIC4.GND, LED1.anode, LED2.anode, LED3.anode, LED4.anode, LED5.anode
  VCC: Ameba1.5V, Tiny_RTC2.VCC, DHT2.NULL, LCM1602_IIC4.VCC, R1.Pin_0
  VSS: LCM1602_IIC4.VSS, LCD5.VSS
  VDD: LCM1602_IIC4.VDD, LCD5.VDD
  N9: LCM1602_IIC4.V0, LCD5.V0
  N10: LCM1602_IIC4.RS, LCD5.RS
  N11: LCM1602_IIC4.RW, LCD5.R/W
  N12: LCM1602_IIC4.E, LCD5.E
  N13: LCM1602_IIC4.D0, LCD5.DB0
  N14: LCM1602_IIC4.D1, LCD5.DB1
  N15: LCM1602_IIC4.D2, LCD5.DB2
  N16: LCM1602_IIC4.D3, LCD5.DB3
  N17: LCM1602_IIC4.D4, LCD5.DB4
  N18: LCM1602_IIC4.D5, LCD5.DB5
  N19: LCM1602_IIC4.D6, LCD5.DB6
  N20: LCM1602_IIC4.D7, LCD5.DB7
  N21: LCM1602_IIC4.A, LCD5.LED+
  N22: LCM1602_IIC4.K, LCD5.LED-
  N23: LCM1602_IIC4.LED_A, LCM1602_IIC4.LED_B
  N24: LED1.cathode, R1.Pin_1
  N25: LED2.cathode, R2.Pin_1
  N26: LED3.cathode, R3.Pin_1
  N27: LED4.cathode, R4.Pin_1
  N28: LED5.cathode, R5.Pin_1

custom parts:
  Ameba: Ameba EVB
  Tiny RTC: Tiny RTC I2C module DS1370Z RTC and AT24C32 EEPROM
  DHT11 Humitidy and Temperature Sensor: DHT11 Humidity and Temperature Sensor
  LCM1602 IIC: I2C-Module to use a 1602 or 2004 LCD on with the wire.h libory Serial LCD Modul
  LCD 20x04: LCD character display, 20 characters by 4 rows. Green.
