# Fritzing sketch 基本電路_RTC_DS1307 (saved by Fritzing 0.9.2b)
breadboards: 1

parts:
  Ameba1 = Ameba
  元件1 = Real Time Clock Module - DS1307 RTC Breakout Board

nets:
  N1: Ameba1.SCL, 元件1.SCL
  N2: Ameba1.SDA, 元件1.SDA
  GND: Ameba1.GND, 元件1.GND
  5V: Ameba1.5V, 元件1.5V

custom parts:
  Ameba: Ameba EVB
