# Fritzing sketch 基本電路_使用光敏電阻控制發光二極體發光強度 (saved by Fritzing 0.9.2b)
breadboards: 1

parts:
  R2 = Resistor [tolerance=±5% resistance=220 package=THT]
  LED2 = LED - 5mm [color="Red (633nm)" package="5 mm [THT]"]
  Ameba2 = Ameba
  R3 = Photocell (LDR) [package=THT]
  R4 = Resistor [tolerance=±5% resistance=4.7k package=THT]

nets:
  N1: R2.Pin_0, Ameba2.GND, R3.pin_0
  N2: R2.Pin_1, LED2.cathode
  N3: LED2.anode, Ameba2.D13
  N4: Ameba2.A0, R3.pin_1, R4.Pin_1
  N5: Ameba2.5V, R4.Pin_0

notes:
  LED GND
  220 Ω
  GND
  LED +5V
  D13
  D7
  D13
  光敏電阻量測電路
  4,7k Ω

custom parts:
  Ameba: Ameba EVB
