# Fritzing sketch 基本電路_切換開發版為無線基地台_有燈號 (saved by Fritzing 0.9.2b)
breadboards: 1

parts:
  Ameba1 = Ameba
  R1 = Resistor [tolerance=±5% resistance=220 package=THT]
  LED1 = LED - 5mm [color="Red (633nm)" package="5 mm [THT]"]

nets:
  N1: Ameba1.D13, LED1.anode
  N2: Ameba1.GND, R1.Pin_0
  N3: R1.Pin_1, LED1.cathode

custom parts:
  Ameba: Ameba EVB
