# Fritzing sketch 基本電路_按鈕(上拉電阻)_整合輸出LED (saved by Fritzing 0.9.2b)
breadboards: 1

parts:
  Ameba1 = Ameba
  R1 = Resistor [tolerance=±5% resistance=4.7k package=THT]
  S1 = Pushbutton [package="[THT]"]
  R2 = Resistor [tolerance=±5% resistance=220 package=THT]
  LED1 = LED - 5mm [color="Red (633nm)" package="5 mm [THT]"]

nets:
  N1: Ameba1.D7, Ameba1.GND, R1.Pin_1, S1.Pin_3, S1.Pin_4, LED1.cathode
  N2: Ameba1.D13, R2.Pin_1
  N3: Ameba1.5V, R1.Pin_0
  N4: S1.Pin_1, S1.Pin_2
  N5: R2.Pin_0, LED1.anode

notes:
  Mini Push Button
  pull-up resistor
  Current limiting resistor
  LED

custom parts:
  Ameba: Ameba EVB
