# Fritzing sketch 基本電路_按鈕(下拉電阻) (saved by Fritzing 0.9.2b)
breadboards: 1

parts:
  Ameba1 = Ameba
  R1 = Resistor [tolerance=±5% resistance=4.7k package=THT]
  S1 = Pushbutton [package="[THT]"]

nets:
  N1: Ameba1.D7, Ameba1.5V, R1.Pin_0, S1.Pin_1, S1.Pin_2, S1.Pin_3, S1.Pin_4
  N2: Ameba1.GND, R1.Pin_1

notes:
  Mini Push Button
  Pull-down resistor

custom parts:
  Ameba: Ameba EVB
