# Fritzing sketch 基本電路_按鈕(下拉電阻)_整合輸出LED (saved by Fritzing 0.9.2b)
breadboards: 1

parts:
  Ameba1 = Ameba
  R1 = Resistor [tolerance=±5% resistance=4.7k package=THT]
  S1 = Pushbutton [package="[THT]"]
  LED2 = LED - 5mm [color="Red (633nm)" package="5 mm [THT]"]
  R3 = Resistor [tolerance=±5% resistance=220 package=THT]

nets:
  N1: Ameba1.D7, Ameba1.5V, R1.Pin_0, S1.Pin_1, S1.Pin_2, S1.Pin_3, S1.Pin_4
  N2: Ameba1.D13, R3.Pin_1
  N3: Ameba1.GND, R1.Pin_1, LED2.cathode
  N4: LED2.anode, R3.Pin_0

notes:
  Mini Push Button
  Pull-down resistor
  Current limiting resistor
  LED

custom parts:
  Ameba: Ameba EVB
