# Fritzing sketch 基本電路_按鈕模組開燈 (saved by Fritzing 0.9.2b)
breadboards: 1

parts:
  Grove2 = Grove Button
  R2 = Resistor [tolerance=±5% resistance=220 package=THT]
  LED2 = LED - 5mm [color="Red (633nm)" package="5 mm [THT]"]
  Ameba2 = Ameba

nets:
  GND: Grove2.GND, R2.Pin_0, Ameba2.GND
  VCC: Grove2.VCC, Ameba2.5V
  N1: Grove2.SIG, Ameba2.D7
  N2: R2.Pin_1, LED2.cathode
  N3: LED2.anode, Ameba2.D13

notes:
  LED GND
  220 Ω
  GND
  LED +5V
  D13
  D7
  D13

custom parts:
  Ameba: Ameba EVB
