# Fritzing sketch 基本電路_按鈕開燈2 (saved by Fritzing 0.9.2b)
breadboards: 1

parts:
  Ameba1 = Ameba
  Grove1 = Grove Button
  R1 = Resistor [tolerance=±5% resistance=220 package=THT]
  LED1 = LED - 5mm [color="Red (633nm)" package="5 mm [THT]"]
  LCM1602_IIC4 = LCM1602 IIC [part_number="LCM1602 IIC" chip_label="LCM1602 IIC" package="DIP (Dual Inline) [THT]"]

nets:
  N1: Ameba1.D7, Grove1.SIG
  N2: Ameba1.D13, LED1.anode
  GND: Ameba1.GND, Grove1.GND, R1.Pin_0, LCM1602_IIC4.GND
  VCC: Ameba1.5V, Grove1.VCC, LCM1602_IIC4.VCC
  N3: R1.Pin_1, LED1.cathode

notes:
  D13
  D7
  LED +5V
  D13
  GND
  LED GND
  220 Ω

custom parts:
  Ameba: Ameba EVB
  LCM1602 IIC: I2C-Module to use a 1602 or 2004 LCD on with the wire.h libory Serial LCD Modul
