# Fritzing sketch 基本電路_紅綠雙燈Led (saved by Fritzing 0.9.2b)
breadboards: 1

parts:
  R3 = Resistor [tolerance=±5% resistance=220 package=THT]
  R4 = Resistor [tolerance=±5% resistance=220 package=THT]
  LED5 = LED - 5mm [color="Red (633nm)" package="5 mm [THT]"]
  LED6 = LED - 5mm [color="Green (560nm)" package="5 mm [THT]"]
  Ameba2 = Ameba

nets:
  N1: R3.Pin_0, LED6.cathode
  N2: R3.Pin_1, Ameba2.D8
  N3: R4.Pin_0, LED5.cathode
  N4: R4.Pin_1, Ameba2.D9
  N5: LED5.anode, LED6.anode, Ameba2.GND

notes:
  LED GND
  220 Ω
  GND
  D8/D9

custom parts:
  Ameba: Ameba EVB
